// Logisim project PIC_tester.circ as structural Verilog: 1 circuit, main circuit main
module main (
  output clk_4,
  output [7:0] W,
  output [2:0] SW,
  output [4:0] RA,
  output [7:0] RB,
  output [12:0] PC,
  output halt
);

  wire comparator_1_eq, counter_1_carry;

  // PIC16F84A pic16f84a_1: pin names not known; wires that end beside it: RA, W, SW, clk_4
  // Probe on PC
  Comparator #(.width(13)) comparator_1 (.a(PC), .b(13'ha), .eq(comparator_1_eq));  // open: gt, lt
  or or_1 (halt, comparator_1_eq, counter_1_carry);
  Counter #(.width(12), .max('hfff), .ongoal("stay")) counter_1 (
    .carry(counter_1_carry), .clk(clk_4));  // open: load, D, count, Q, clr
endmodule
