// Logisim project Arithmetic_logic_units.circ as structural Verilog: 4 circuits, main circuit Test
module Test (
);

  wire alu_1_sw_w, clock_1_out, clock_2_out, clock_3_out, CLR, comparator_1_eq, controlled_buffer_1_out,
       not_1_out;
  wire [7:0] OP;
  wire [12:0] RESULTS;
  wire [25:0] ram_1_data;

  Button u_CLR (.out(CLR));
  Clock clock_1 (.out(clock_1_out));
  Counter counter_1 (.Q(OP), .clk(controlled_buffer_1_out), .clr(CLR));  // open: load, D, count, carry
  assign controlled_buffer_1_out = not_1_out ? clock_2_out : 1'bz;  // Controlled_Buffer controlled_buffer_1
  Comparator comparator_1 (.a(8'h2f), .b(OP), .eq(comparator_1_eq));  // open: gt, lt
  not not_1 (not_1_out, comparator_1_eq);
  RAM #(.dataWidth(26)) ram_1 (.addr(OP), .data(ram_1_data), .sel(1'b1), .clk(clock_1_out), .ld(1'b1));  // open: clr
  // Probe on ram_1_data
  Clock clock_2 (.out(clock_2_out));
  // Probe on ram_1_data[7:0]
  // Probe on ram_1_data[10:8]
  // Probe on ram_1_data[18:11]
  // Probe on ram_1_data[24:19]
  // Probe on ram_1_data[25]
  // Probe on RESULTS[7:0]
  // Probe on RESULTS[10:8]
  // Probe on RESULTS[11]
  // Probe on alu_1_sw_w
  // Probe on RESULTS[12]
  // Probe on ram_1_data[7:0]
  // Probe on ram_1_data[10:8]
  // Probe on ram_1_data[18:11]
  // Probe on ram_1_data[24:19]
  ALU alu_1 (
    .Z_DC_C(ram_1_data[10:8]), .DATA(ram_1_data[7:0]), .W(ram_1_data[18:11]), .OP_7(ram_1_data[25]),
    .SEL(ram_1_data[24:19]), .destf(RESULTS[11]), .Skip(RESULTS[12]), .sw_w(alu_1_sw_w),
    .Z_DC_C_out(RESULTS[10:8]), .OUTPUT(RESULTS[7:0]));  // open: Control, Call_Goto
  // Probe on RESULTS
  Clock clock_3 (.out(clock_3_out));
  RAM #(.dataWidth(13)) ram_2 (.addr(OP), .data(RESULTS), .sel(1'b1), .clk(clock_3_out), .ld(1'b0), .clr(CLR));

  // Notes on the sheet:
  //   PROGRAM
  //   Sequence
  //   STATUS=Z,DC,C
  //   ALU
  //   SAVE RUN
endmodule

module ALU (
  input  [2:0] Z_DC_C,
  input  [7:0] DATA,
  input  [7:0] W,
  input  OP_7,
  input  [5:0] SEL,
  output Control,
  output [1:0] Call_Goto,
  output Skip,
  output sw_w,
  output [2:0] Z_DC_C_out,
  output [7:0] OUTPUT,
  output destf
);

  wire and_1_out, and_4_out, decoder_1_out0, decoder_1_out1, decoder_1_out2, decoder_1_out3, not_1_out,
       not_2_out, or_1_out;
  wire [3:0] OP_lit;

  Decoder #(.select(2), .enable("false")) decoder_1 (
    .out0(decoder_1_out0), .out1(decoder_1_out1), .out2(decoder_1_out2), .out3(decoder_1_out3), .sel(SEL[5:4]));
  // Probe on SEL[5:4]
  assign {OUTPUT, Z_DC_C_out, sw_w, Skip} = or_1_out ? {W, Z_DC_C, 2'b00} : 13'bz;  // Controlled_Buffer controlled_buffer_1
  or or_1 (or_1_out, Control, decoder_1_out2);
  Comparator #(.width(7)) comparator_1 (.a({7{1'b0}}), .b({OP_7, SEL}), .eq(Control));  // open: gt, lt
  not not_1 (not_1_out, Control);
  and and_1 (and_1_out, decoder_1_out0, not_1_out);
  // Probe on W
  // Probe on W
  // Probe on SEL[3:0]
  // Probe on DATA
  // Probe on DATA
  // Probe on Skip
  // Probe on Z_DC_C
  ALU_Byte alu_byte_1 (
    .C_DC_Z_in(Z_DC_C), .Skip(Skip), .W(W), .DATA(DATA), .OUT(OUTPUT), .SEL(SEL[3:0]), .EN(and_1_out),
    .C_DC_Z(Z_DC_C_out), .sw_w(sw_w));
  assign {sw_w, Z_DC_C_out} = decoder_1_out1 ? {1'b0, Z_DC_C} : 4'bz;  // Controlled_Buffer controlled_buffer_2
  // Probe on DATA
  // Probe on SEL[3:2]
  ALU_Bit alu_bit_1 (
    .BIT({SEL[1:0], OP_7}), .HO(SEL[3:2]), .DATA(DATA), .OUT(OUTPUT), .Skip(Skip), .EN(decoder_1_out1));
  // Probe on {SEL[1:0], OP_7}
  // Probe on Skip
  not not_2 (not_2_out, SEL[3]);
  and and_2 (Call_Goto[1], not_2_out, decoder_1_out2);
  and and_3 (Call_Goto[0], SEL[3], decoder_1_out2);
  and and_4 (and_4_out, and_1_out, OP_7);
  or or_2 (destf, decoder_1_out1, and_4_out);
  // Probe on DATA
  // Probe on Z_DC_C
  // Probe on OP_lit
  // Probe on DATA
  // Probe on W
  // Probe on W
  // Probe on Skip
  ALU_Byte alu_byte_2 (
    .C_DC_Z_in(Z_DC_C), .Skip(Skip), .W(DATA), .DATA(W), .OUT(OUTPUT), .SEL(OP_lit), .EN(decoder_1_out3),
    .C_DC_Z(Z_DC_C_out), .sw_w(sw_w));
  ROM #(.addrWidth(4), .dataWidth(4)) rom_1 (.addr(SEL[3:0]), .data(OP_lit), .sel(1'b1));

  // Other names for the same wires on the sheet: OP_sel[3:0] = SEL[3:0]

  // Notes on the sheet:
  //   Chip selection
  //   Control
  //   CLRWDT 0110 0100
  //   SLEEP 0110 0011
  //   RETIE 0000 1001
  //   RETURN 0000 1000
  //   Byte Oriented
  //   MOVWF 0000
  //   CLRF 0001
  //   SUBWF 0010
  //   DECF 0011
  //   IORWF 0100
  //   ANDF 0101
  //   XORWF 0110
  //   ADDF 0111
  //   Byte Oriented
  //   MOVF 1000
  //   COMF 1001
  //   INCF 1010
  //   DECFSZ 1011
  //   RRF1100
  //   RLF 1101
  //   SWAPF 1110
  //   INCFSZ 1111
  //   Bit Oriented
  //   Bit Oriented
  //   BCF 0100
  //   BSF 0101
  //   BTFSC 0110
  //   BTFSS 0111
  //   Jumps
  //   Jumps
  //   CALL 0
  //   GOTO 1
  //   Litteral
  //   Litteral
  //   Litteral
  //   MOVLW 00xx
  //   RETLW 01xx
  //   IORLW 1000
  //   ANDLW1001
  //   destination
  //   contents of rom_1 (hex, n*v repeats v):
  //   8*0 8 9 a 0 2 2 7 7
  //   XORLW 1010
  //   NOP 1011
  //   SUBLW 110x
  //   ADDLW 111x
endmodule

module ALU_Byte (
  input  [7:0] W,
  input  [7:0] DATA,
  input  [2:0] C_DC_Z_in,
  input  [3:0] SEL,
  input  EN,
  output Skip,
  output [2:0] C_DC_Z,
  output sw_w,
  output [7:0] OUT
);

  wire adder_3_cout, B, C, comparator_1_eq, not_1_out, not_4_out, not_5_out, subtractor_1_bout,
       subtractor_3_bout;
  wire [7:0] adder_1_out, and_1_out, multiplexer_6_out, not_3_out, or_1_out, SD, shifter_1_out,
       shifter_2_out, shifter_3_out, shifter_4_out, SI, subtractor_1_out, xor_1_out;

  // Probe on 1'b0
  // Probe on 1'b1
  Comparator comparator_1 (.a(DATA), .b(W), .eq(comparator_1_eq));  // open: gt, lt
  Multiplexer #(.select(4)) multiplexer_1 (
    .in0(C_DC_Z_in[0]), .in1(comparator_1_eq), .in2(comparator_1_eq), .in3(comparator_1_eq),
    .in4(comparator_1_eq), .in5(comparator_1_eq), .in6(comparator_1_eq), .in7(comparator_1_eq),
    .in8(comparator_1_eq), .in9(comparator_1_eq), .in10(comparator_1_eq), .in11(C_DC_Z_in[0]),
    .in12(comparator_1_eq), .in13(comparator_1_eq), .in14(C_DC_Z_in[0]), .in15(C_DC_Z_in[0]),
    .out(C_DC_Z[0]), .sel(SEL), .en(EN));
  // Probe on 1'b1
  Multiplexer #(.select(4)) multiplexer_2 (
    .in0(1'b0), .in1(1'b1), .in2(1'b1), .in3(1'b1), .in4(1'b1), .in5(1'b1), .in6(1'b1), .in7(1'b1),
    .in8(1'b1), .in9(1'b1), .in10(1'b1), .in11(1'b0), .in12(1'b1), .in13(1'b1), .in14(1'b0), .in15(1'b0),
    .out(sw_w), .sel(SEL), .en(EN));
  // Probe on 1'b1
  // Probe on 1'b1
  // Probe on 1'b1
  // Probe on 1'b1
  // Probe on 1'b1
  // Probe on 1'b1
  // Probe on 1'b1
  not not_1 (not_1_out, C_DC_Z_in[2]);
  Adder adder_1 (.a(DATA), .b(W), .out(adder_1_out), .cin(C_DC_Z_in[2]), .cout(C));
  not not_2 (B, subtractor_1_bout);
  Adder adder_2 (.a(DATA), .b(8'h1), .out(SI), .cin(1'b0));  // open: cout
  // Probe on C_DC_Z[0]
  // Probe on 1'b1
  // Probe on 1'b1
  // Probe on 1'b1
  // Probe on 1'b0
  // Probe on 1'b0
  // Probe on 1'b0
  // Probe on W
  Subtractor subtractor_1 (.a(DATA), .b(W), .out(subtractor_1_out), .bin(not_1_out), .bout(subtractor_1_bout));
  assign or_1_out = W | DATA;  // OR_Gate or_1, 8 bits wide
  Subtractor subtractor_2 (.a(DATA), .b(8'h1), .out(SD), .bin(1'b0));  // open: bout
  assign not_3_out = ~DATA;  // NOT_Gate not_3, 8 bits wide
  assign xor_1_out = W ^ DATA;  // XOR_Gate xor_1, 8 bits wide
  assign and_1_out = W & DATA;  // AND_Gate and_1, 8 bits wide
  // Probe on OUT
  Multiplexer #(.select(4), .width(8)) multiplexer_3 (
    .in0(W), .in1({8{1'b0}}), .in2(subtractor_1_out), .in3(SD), .in4(or_1_out), .in5(and_1_out),
    .in6(xor_1_out), .in7(adder_1_out), .in8(DATA), .in9(not_3_out), .in10(SI), .in11(SD),
    .in12(shifter_2_out), .in13(shifter_4_out), .in14({DATA[3:0], DATA[7:4]}), .in15(SI), .out(OUT),
    .sel(SEL), .en(EN));
  // Probe on OUT
  // Probe on DATA
  Shifter #(.shift("rr")) shifter_1 (.in(DATA), .\dist (3'b001), .out(shifter_1_out));
  Shifter #(.shift("lr")) shifter_2 (.in(DATA), .\dist (3'b001), .out(shifter_2_out));
  Shifter #(.shift("rl")) shifter_3 (.in(DATA), .\dist (3'b001), .out(shifter_3_out));
  Shifter shifter_4 (.in(DATA), .\dist (3'b001), .out(shifter_4_out));
  // Probe on C_DC_Z[2]
  Multiplexer #(.select(4)) multiplexer_4 (
    .in0(C_DC_Z_in[2]), .in1(C_DC_Z_in[2]), .in2(B), .in3(C_DC_Z_in[2]), .in4(C_DC_Z_in[2]),
    .in5(C_DC_Z_in[2]), .in6(C_DC_Z_in[2]), .in7(C), .in8(C_DC_Z_in[2]), .in9(C_DC_Z_in[2]),
    .in10(C_DC_Z_in[2]), .in11(C_DC_Z_in[2]), .in12(shifter_3_out[0]), .in13(shifter_1_out[7]),
    .in14(C_DC_Z_in[2]), .in15(C_DC_Z_in[2]), .out(C_DC_Z[2]), .sel(SEL), .en(EN));
  // Probe on C_DC_Z_in[2]
  not not_4 (not_4_out, C_DC_Z_in[2]);
  Adder #(.width(4)) adder_3 (.a(DATA[3:0]), .b(W[3:0]), .cin(C_DC_Z_in[2]), .cout(adder_3_cout));  // open: out
  not not_5 (not_5_out, subtractor_3_bout);
  Multiplexer #(.select(4)) multiplexer_5 (
    .in0(C_DC_Z_in[1]), .in1(C_DC_Z_in[1]), .in2(not_5_out), .in3(C_DC_Z_in[1]), .in4(C_DC_Z_in[1]),
    .in5(C_DC_Z_in[1]), .in6(C_DC_Z_in[1]), .in7(adder_3_cout), .in8(C_DC_Z_in[1]), .in9(C_DC_Z_in[1]),
    .in10(C_DC_Z_in[1]), .in11(C_DC_Z_in[1]), .in12(C_DC_Z_in[1]), .in13(C_DC_Z_in[1]), .in14(C_DC_Z_in[1]),
    .in15(C_DC_Z_in[1]), .out(C_DC_Z[1]), .sel(SEL), .en(EN));
  Subtractor #(.width(4)) subtractor_3 (
    .a(DATA[3:0]), .b(W[3:0]), .bin(not_4_out), .bout(subtractor_3_bout));  // open: out
  // Probe on C_DC_Z_in[1]
  // Probe on C_DC_Z[1]
  Multiplexer #(.select(4), .width(8)) multiplexer_6 (
    .in0(8'h10), .in1(8'h10), .in2(8'h10), .in3(8'h10), .in4(8'h10), .in5(8'h10), .in6(8'h10), .in7(8'h10),
    .in8(8'h10), .in9(8'h10), .in10(8'h10), .in11(SD), .in12(8'h10), .in13(8'h10), .in14(8'h10), .in15(SI),
    .out(multiplexer_6_out), .sel(SEL), .en(EN));
  // Probe on 8'h10
  Comparator comparator_2 (.a(multiplexer_6_out), .b({8{1'b0}}), .eq(Skip));  // open: gt, lt

  // Other names for the same wires on the sheet: Z_in = C_DC_Z_in[0]; DC_in = C_DC_Z_in[1]; C_in = C_DC_Z_in[2]

  // Notes on the sheet:
  //   Byte/litteral oriented chip
endmodule

module ALU_Bit (
  input  [7:0] DATA,
  input  [2:0] BIT,
  input  [1:0] HO,
  input  EN,
  output [7:0] OUT,
  output Skip
);

  wire and_1_out, bitselector_1_out, decoder_1_out0, decoder_1_out1, decoder_1_out2, decoder_1_out3,
       decoder_1_out4, decoder_1_out5, decoder_1_out6, decoder_1_out7, nor_1_out, not_1_out, or_1_out;
  wire [7:0] multiplexer_1_out;

  // Probe on HO[0]
  // Probe on BIT
  // Probe on HO
  Multiplexer #(.enable("false")) multiplexer_1 (
    .in0(DATA[0]), .in1(HO[0]), .out(multiplexer_1_out[0]), .sel(decoder_1_out0));
  Decoder #(.select(3), .enable("false")) decoder_1 (
    .out0(decoder_1_out0), .out1(decoder_1_out1), .out2(decoder_1_out2), .out3(decoder_1_out3),
    .out4(decoder_1_out4), .out5(decoder_1_out5), .out6(decoder_1_out6), .out7(decoder_1_out7), .sel(BIT));
  // Probe on BIT
  Multiplexer #(.enable("false")) multiplexer_2 (
    .in0(DATA[1]), .in1(HO[0]), .out(multiplexer_1_out[1]), .sel(decoder_1_out1));
  Multiplexer #(.enable("false")) multiplexer_3 (
    .in0(DATA[2]), .in1(HO[0]), .out(multiplexer_1_out[2]), .sel(decoder_1_out2));
  // Probe on HO[1]
  // Probe on DATA
  // Probe on DATA
  Multiplexer #(.enable("false")) multiplexer_4 (
    .in0(DATA[3]), .in1(HO[0]), .out(multiplexer_1_out[3]), .sel(decoder_1_out3));
  Multiplexer #(.enable("false")) multiplexer_5 (
    .in0(DATA[4]), .in1(HO[0]), .out(multiplexer_1_out[4]), .sel(decoder_1_out4));
  // Probe on multiplexer_1_out
  // Probe on DATA
  not not_1 (not_1_out, HO[1]);
  Multiplexer #(.width(8)) multiplexer_6 (.in0(DATA), .in1(multiplexer_1_out), .out(OUT), .sel(not_1_out), .en(EN));
  Multiplexer #(.enable("false")) multiplexer_7 (
    .in0(DATA[5]), .in1(HO[0]), .out(multiplexer_1_out[5]), .sel(decoder_1_out5));
  Multiplexer #(.enable("false")) multiplexer_8 (
    .in0(DATA[6]), .in1(HO[0]), .out(multiplexer_1_out[6]), .sel(decoder_1_out6));
  Multiplexer #(.enable("false")) multiplexer_9 (
    .in0(DATA[7]), .in1(HO[0]), .out(multiplexer_1_out[7]), .sel(decoder_1_out7));
  // Probe on BIT
  nor nor_1 (nor_1_out, bitselector_1_out, HO[0]);
  or or_1 (or_1_out, nor_1_out, and_1_out);
  Multiplexer multiplexer_10 (.in0(1'b0), .in1(or_1_out), .out(Skip), .sel(HO[1]), .en(EN));
  BitSelector bitselector_1 (.in(DATA), .out(bitselector_1_out), .sel(BIT));
  and and_1 (and_1_out, bitselector_1_out, HO[0]);
  // Probe on nor_1_out
  // Probe on and_1_out

  // Other names for the same wires on the sheet: Bit_sel[2:0] = BIT
endmodule
