// Logisim project PIC_registers.circ as structural Verilog: 9 circuits, main circuit async_register
// io_in
module tester (
);

  wire button_1_out, JMP_out, not_1_out, or_1_out, t_ff_1_q;
  wire [1:0] CLK_out;
  wire [3:3] control;
  wire [4:0] ram_1_tmr0_io_int_2;
  wire [6:0] counter_1_q;
  wire [7:0] ram_1_data_bus_out, ram_1_eeprom_out, ram_1_eeprom_out_2, ram_1_eeprom_out_3, ram_1_sfr_out,
       ram_1_sfr_out_2, ram_1_sfr_out_3, ram_1_sfr_out_4, ram_1_tmr0_io_int, ram_1_tmr0_io_int_3;
  wire [12:0] ram_1_pc;

  // Probe on ram_1_pc
  // Probe on ram_1_eeprom_out
  // Probe on ram_1_eeprom_out_2
  // Probe on ram_1_eeprom_out_3
  // Probe on ram_1_sfr_out
  // Probe on ram_1_sfr_out_2
  // Probe on ram_1_sfr_out_3
  // Probe on ram_1_sfr_out_4
  // Probe on ram_1_tmr0_io_int
  // Probe on ram_1_tmr0_io_int_2
  // Probe on ram_1_tmr0_io_int_3
  or or_1 (or_1_out, 1'b0, 1'b0, 1'b0, JMP_out);
  Button JMP (.out(JMP_out));
  Counter #(.width(7), .max('h7f)) counter_1 (
    .count(not_1_out), .Q(counter_1_q), .clk(CLK_out[0]), .clr(CLK_out[1]));  // open: load, D, carry
  not not_1 (not_1_out, or_1_out);
  Clock CLK (.out(CLK_out[0]));
  // Probe on ram_1_data_bus_out
  // Probe on ram_1_data_bus_out
  Button RST (.out(CLK_out[1]));
  RAM ram_1 (
    .DATA_BUS_OUT(ram_1_data_bus_out), .PC(ram_1_pc),
    .EEPROM_out({ram_1_eeprom_out_3, ram_1_eeprom_out_2, ram_1_eeprom_out}),
    .SFR_out({ram_1_sfr_out_4, ram_1_sfr_out_3, ram_1_sfr_out_2, ram_1_sfr_out}),
    .Control_in({3'b001, control[3], 3'b001}), .EEPROM_in({16{1'b0}}), .IO_in(13'hfff), .SW_in(8'h18),
    .WE(1'b1), .CLK_RST(CLK_out), .ADDRESS(counter_1_q), .DATA_BUS(ram_1_data_bus_out),
    .TMR0_IO_INT({ram_1_tmr0_io_int_3, ram_1_tmr0_io_int_2, ram_1_tmr0_io_int}));
  assign ram_1_data_bus_out = 1'b1 ? 8'h3f : 8'bz;  // Controlled_Buffer controlled_buffer_1
  // Probe on 8'h3f
  // Probe on 8'h3f
  // Probe on 1'b1
  // Probe on 13'hfff
  // Probe on 8'h18
  T_Flip_Flop t_ff_1 (.clk(CLK_out[0]), .T(button_1_out), .Q(t_ff_1_q), .en(1'b1));  // open: Qn, preset, reset
  Button button_1 (.out(button_1_out));
  // Probe on 1'b1
  // Probe on 1'b0
  // Probe on 1'b0
  Button intf (.out(control[3]));
  // Probe on 3'b001
endmodule

module RAM (
  input  [7:0] DATA_BUS,
  input  [6:0] Control_in,
  input  [15:0] EEPROM_in,
  input  [12:0] IO_in,
  input  [7:0] SW_in,
  input  [6:0] ADDRESS,
  input  WE,
  input  [1:0] CLK_RST,
  output [7:0] DATA_BUS_OUT,
  output [12:0] PC,
  output [23:0] EEPROM_out,
  output [31:0] SFR_out,
  output [20:0] TMR0_IO_INT
);

  wire and_1_out, and_2_out, and_3_out, and_4_out, buffer_3_out, buffer_4_out, comparator_1_eq,
       comparator_2_gt, comparator_3_eq, comparator_4_eq, INT_W, not_1_out, not_2_out, not_3_out, not_4_out,
       not_5_out, not_6_out, or_2_out, RBIF, T0IF;
  wire [1:0] buffer_2_out;
  wire [2:0] clock_1_out;
  wire [6:0] multiplexer_1_out, multiplexer_2_out, subtractor_1_out;
  wire [7:0] INT_IN, TRISA, TRISB;
  wire [7:5] PCLATH, porta_reg_1_out;

  // Probe on subtractor_1_out
  not not_1 (not_1_out, WE);
  Comparator #(.width(7)) comparator_1 (.a(ADDRESS), .b({7{1'b0}}), .eq(comparator_1_eq));  // open: gt, lt
  // Probe on PC[7:0]
  // Probe on SFR_out[15:8]
  // Probe on SFR_out[7:0]
  // Probe on {PCLATH, PC[12:8]}
  // Probe on SFR_out[23:16]
  Subtractor #(.width(7)) subtractor_1 (.a(ADDRESS), .b(7'b0001100), .out(subtractor_1_out), .bin(1'b0));  // open: bout
  Comparator #(.width(7), .mode("unsigned")) comparator_2 (
    .a(ADDRESS), .b(7'b0001011), .gt(comparator_2_gt));  // open: eq, lt
  and and_1 (and_1_out, not_1_out, comparator_1_eq);
  assign DATA_BUS_OUT = and_1_out ? {8{1'b0}} : 8'bz;  // Controlled_Buffer controlled_buffer_1
  async_register async_register_1 (
    .SYNCH_ADDRESS(ADDRESS), .DIRECT_ADDRESS(7'b0000010), .BUS_OUT(DATA_BUS_OUT), .BUS_IN(DATA_BUS),
    .OUT(PC[7:0]), .WREG_CLK_RST({WE, CLK_RST}), .WE_async(1'b0));  // open: AsynchronousW
  STATUS status_1 (
    .SYNCH_ADDRESS(ADDRESS), .DIRECT_ADDRESS(7'b0000011), .BUS_OUT(DATA_BUS_OUT), .BUS_IN(DATA_BUS),
    .SW_IN(SW_in), .OUT(SFR_out[15:8]), .WREG_CLK_RST({WE, CLK_RST}), .async_w(Control_in[1]));
  async_register async_register_2 (
    .SYNCH_ADDRESS(ADDRESS), .DIRECT_ADDRESS(7'b0000100), .BUS_OUT(DATA_BUS_OUT), .BUS_IN(DATA_BUS),
    .OUT(SFR_out[7:0]), .WREG_CLK_RST({WE, CLK_RST}), .WE_async(1'b0));  // open: AsynchronousW
  async_register async_register_3 (
    .SYNCH_ADDRESS(ADDRESS), .DIRECT_ADDRESS(7'b0001010), .BUS_OUT(DATA_BUS_OUT), .BUS_IN(DATA_BUS),
    .OUT({PCLATH, PC[12:8]}), .WREG_CLK_RST({WE, CLK_RST}), .WE_async(1'b0));  // open: AsynchronousW
  async_register async_register_4 (
    .SYNCH_ADDRESS(ADDRESS), .DIRECT_ADDRESS(7'b0001011), .BUS_OUT(DATA_BUS_OUT), .BUS_IN(DATA_BUS),
    .AsynchronousW(INT_IN), .OUT(SFR_out[23:16]), .WREG_CLK_RST({WE, CLK_RST}), .WE_async(INT_W));
  // Probe on INT_IN
  and and_2 (and_2_out, comparator_2_gt, WE);
  assign DATA_BUS_OUT = and_2_out ? DATA_BUS : 8'bz;  // Controlled_Buffer controlled_buffer_2
  RAM_part #(.addrWidth(7)) ram_1 (
    .addr(subtractor_1_out), .data(DATA_BUS_OUT), .sel(comparator_2_gt), .clk(CLK_RST[0]), .ld(not_2_out),
    .clr(CLK_RST[1]));
  not not_2 (not_2_out, WE);
  // Probe on multiplexer_1_out
  not not_3 (not_3_out, SFR_out[13]);
  Multiplexer #(.width(7), .enable("false")) multiplexer_1 (
    .in0({7{1'b0}}), .in1(ADDRESS), .out(multiplexer_1_out), .sel(not_3_out));
  // Probe on DATA_BUS_OUT
  TIMR0 timr0_1 (
    .SYNCH_ADDRESS(multiplexer_1_out), .DIRECT_ADDRESS(7'b0000001), .BUS_OUT(DATA_BUS_OUT),
    .BUS_IN(DATA_BUS), .T0IF(T0IF), .WREG_CLK_RST({WE, CLK_RST}), .RATE(Control_in[0]),
    .TIMR0(TMR0_IO_INT[7:0]));
  // Probe on TMR0_IO_INT[7:0]
  // Probe on {porta_reg_1_out, TMR0_IO_INT[12:8]}
  PORTA_reg porta_reg_1 (
    .BUS_IN(DATA_BUS), .SYNCH_ADDRESS(multiplexer_1_out), .DIRECT_ADDRESS(7'b0000101), .TRISA(TRISA),
    .BUS_OUT(DATA_BUS_OUT), .PIN_IN(IO_in[4:0]), .OUT({porta_reg_1_out, TMR0_IO_INT[12:8]}),
    .WREG_CLK_RST({WE, CLK_RST}));
  PORTB_reg portb_reg_1 (
    .BUS_IN(DATA_BUS), .SYNCH_ADDRESS(multiplexer_1_out), .DIRECT_ADDRESS(7'b0000110), .RBIF(RBIF),
    .WREG_CLK_RST({WE, CLK_RST}), .TRISB(TRISB), .BUS_OUT(DATA_BUS_OUT), .PIN_IN(IO_in[12:5]),
    .OUT(TMR0_IO_INT[20:13]));
  // Probe on TMR0_IO_INT[20:13]
  not not_4 (not_4_out, WE);
  Comparator #(.width(7)) comparator_3 (.a(multiplexer_1_out), .b(7'b0000111), .eq(comparator_3_eq));  // open: gt, lt
  // Probe on EEPROM_out[7:0]
  async_register async_register_5 (
    .SYNCH_ADDRESS(multiplexer_1_out), .DIRECT_ADDRESS(7'b0001000), .BUS_OUT(DATA_BUS_OUT),
    .BUS_IN(DATA_BUS), .AsynchronousW(EEPROM_in[7:0]), .OUT(EEPROM_out[7:0]), .WREG_CLK_RST({WE, CLK_RST}),
    .WE_async(Control_in[5]));
  // Probe on EEPROM_out[15:8]
  async_register async_register_6 (
    .SYNCH_ADDRESS(multiplexer_1_out), .DIRECT_ADDRESS(7'b0001001), .BUS_OUT(DATA_BUS_OUT),
    .BUS_IN(DATA_BUS), .OUT(EEPROM_out[15:8]), .WREG_CLK_RST({WE, CLK_RST}), .WE_async(1'b0));  // open: AsynchronousW
  Pull_Resistor pull_resistor_1 (.node(Control_in[3]));
  and and_3 (and_3_out, not_4_out, comparator_3_eq);
  assign DATA_BUS_OUT = and_3_out ? {8{1'b0}} : 8'bz;  // Controlled_Buffer controlled_buffer_3
  assign INT_IN[6:3] = SFR_out[22:19];  // Buffer buffer_1, 4 bits wide
  assign buffer_2_out = {SFR_out[18], SFR_out[16]};  // Buffer buffer_2, 2 bits wide
  buf buffer_3 (buffer_3_out, SFR_out[17]);
  buf buffer_4 (buffer_4_out, SFR_out[23]);
  T_Flip_Flop #(.trigger("falling")) t_ff_1 (
    .clk(CLK_RST[0]), .T(Control_in[2]), .reset(WE), .en(1'b1));  // open: Q, Qn, preset
  // Probe on multiplexer_2_out
  Multiplexer #(.width(7), .enable("false")) multiplexer_2 (
    .in0({7{1'b0}}), .in1(ADDRESS), .out(multiplexer_2_out), .sel(SFR_out[13]));
  or or_1 (INT_W, RBIF, T0IF, Control_in[3], Control_in[2]);
  // Probe on SFR_out[31:24]
  async_register async_register_7 (
    .SYNCH_ADDRESS(multiplexer_2_out), .DIRECT_ADDRESS(7'b0000001), .BUS_OUT(DATA_BUS_OUT),
    .BUS_IN(DATA_BUS), .OUT(SFR_out[31:24]), .WREG_CLK_RST({WE, CLK_RST}), .WE_async(1'b0));  // open: AsynchronousW
  async_register async_register_8 (
    .SYNCH_ADDRESS(multiplexer_2_out), .DIRECT_ADDRESS(7'b0000101), .BUS_OUT(DATA_BUS_OUT),
    .BUS_IN(DATA_BUS), .OUT(TRISA), .WREG_CLK_RST({WE, CLK_RST}), .WE_async(1'b0));  // open: AsynchronousW
  // Probe on TRISA
  async_register async_register_9 (
    .SYNCH_ADDRESS(multiplexer_2_out), .DIRECT_ADDRESS(7'b0000110), .BUS_OUT(DATA_BUS_OUT),
    .BUS_IN(DATA_BUS), .OUT(TRISB), .WREG_CLK_RST({WE, CLK_RST}), .WE_async(1'b0));  // open: AsynchronousW
  // Probe on TRISB
  not not_5 (not_5_out, WE);
  Comparator #(.width(7)) comparator_4 (.a(multiplexer_2_out), .b(7'b0000111), .eq(comparator_4_eq));  // open: gt, lt
  and and_4 (and_4_out, not_5_out, comparator_4_eq);
  async_register async_register_10 (
    .SYNCH_ADDRESS(multiplexer_2_out), .DIRECT_ADDRESS(7'b0001000), .BUS_OUT(DATA_BUS_OUT),
    .BUS_IN(DATA_BUS), .AsynchronousW(EEPROM_in[15:8]), .OUT(EEPROM_out[23:16]),
    .WREG_CLK_RST({WE, CLK_RST}), .WE_async(Control_in[6]));
  // Probe on EEPROM_out[23:16]
  or or_2 (or_2_out, RBIF, T0IF);
  not not_6 (not_6_out, buffer_4_out);
  assign DATA_BUS_OUT = and_4_out ? {8{1'b0}} : 8'bz;  // Controlled_Buffer controlled_buffer_4
  // Probe on ADDRESS
  // Probe on ADDRESS
  Multiplexer #(.width(2), .enable("false")) multiplexer_3 (
    .in0(buffer_2_out), .in1({T0IF, RBIF}), .out({INT_IN[2], INT_IN[0]}), .sel(or_2_out));
  Multiplexer #(.enable("false")) multiplexer_4 (
    .in0(buffer_3_out), .in1(Control_in[3]), .out(INT_IN[1]), .sel(Control_in[3]));
  Multiplexer #(.enable("false")) multiplexer_5 (
    .in0(buffer_4_out), .in1(not_6_out), .out(INT_IN[7]), .sel(Control_in[2]));
  Button RST (.out(clock_1_out[1]));
  Clock clock_1 (.out(clock_1_out[0]));
  Button u_WE (.out(clock_1_out[2]));

  // Other names for the same wires on the sheet: PORTA[4:0] = TMR0_IO_INT[12:8]; TIMR_W = Control_in[0];
  //   SW_E = Control_in[1]; EGIE = Control_in[2]; INTF = Control_in[3]; EEIF = Control_in[4]; DAT_W = Control_in[5];
  //   ECON_W = Control_in[6]; EEDATA_in[7:0] = EEPROM_in[7:0]; EECON1_in[7:0] = EEPROM_in[15:8];
  //   EEDATA[7:0] = EEPROM_out[7:0]; EEADR[7:0] = EEPROM_out[15:8]; EECON1[7:0] = EEPROM_out[23:16];
  //   PIN_A[4:0] = IO_in[4:0]; PIN_B[7:0] = IO_in[12:5]; PCL[7:0] = PC[7:0]; PCLATH[4:0] = PC[12:8];
  //   FSR[7:0] = SFR_out[7:0]; STATUS[7:0] = SFR_out[15:8]; RP0 = SFR_out[13]; INTCON[7:0] = SFR_out[23:16];
  //   OPT[7:0] = SFR_out[31:24]; SW[7:0] = SW_in; TIMR0[7:0] = TMR0_IO_INT[7:0]; PORTB[7:0] = TMR0_IO_INT[20:13]

  // Notes on the sheet:
  //   PCL reg
  //   STATUS reg
  //   FSR reg
  //   PCLATH reg
  //   INTCON reg
  //   RAM GFR
  //   68x8
  //   TIMR0 reg
  //   PORTA reg
  //   PORTB reg
  //   EEDATA reg
  //   EEADR reg
  //   Bank 0
  //   EECON2
  //   INTERRUPT FLAGS HANDLING
  //   OPTION reg
  //   TRISA reg
  //   TRISB reg
  //   EECON1 reg
  //   Bank 1
  //   T0IF
  //   RBIF
  //   INTF
  //   GEIE
endmodule

module TIMR0 (
  input  [6:0] SYNCH_ADDRESS,
  input  [7:0] BUS_IN,
  input  [6:0] DIRECT_ADDRESS,
  input  [2:0] WREG_CLK_RST,
  input  RATE,
  output [7:0] BUS_OUT,
  output [7:0] TIMR0,
  output T0IF
);

  wire and_1_out, and_2_out, button_1_out, comparator_1_eq, not_1_out, not_2_out;
  wire [1:1] clock_1_out;

  not not_1 (not_1_out, WREG_CLK_RST[2]);
  Comparator #(.width(7)) comparator_1 (.a(SYNCH_ADDRESS), .b(DIRECT_ADDRESS), .eq(comparator_1_eq));  // open: gt, lt
  Clock clock_1 (.out(clock_1_out[1]));
  and and_1 (and_1_out, comparator_1_eq, not_1_out);
  and and_2 (and_2_out, comparator_1_eq, WREG_CLK_RST[2], not_2_out);
  not not_2 (not_2_out, RATE);
  Button button_1 (.out(button_1_out));
  assign BUS_OUT = and_1_out ? TIMR0 : 8'bz;  // Controlled_Buffer controlled_buffer_1
  Counter counter_1 (
    .load(and_2_out), .D(BUS_IN), .count(RATE), .Q(TIMR0), .carry(T0IF), .clk(WREG_CLK_RST[0]),
    .clr(WREG_CLK_RST[1]));
endmodule

module STATUS (
  input  [6:0] SYNCH_ADDRESS,
  input  [6:0] DIRECT_ADDRESS,
  input  [7:0] BUS_IN,
  input  [7:0] SW_IN,
  input  [2:0] WREG_CLK_RST,
  input  async_w,
  output [7:0] OUT,
  output [7:0] BUS_OUT
);

  wire and_1_out, and_2_out, buffer_1_out, comparator_1_eq, not_1_out, or_1_out;
  wire [5:0] multiplexer_2_out;

  and and_1 (and_1_out, comparator_1_eq, not_1_out);
  not not_1 (not_1_out, WREG_CLK_RST[2]);
  Comparator #(.width(7)) comparator_1 (.a(SYNCH_ADDRESS), .b(DIRECT_ADDRESS), .eq(comparator_1_eq));  // open: gt, lt
  and and_2 (and_2_out, comparator_1_eq, WREG_CLK_RST[2]);
  // Probe on {2'b00, multiplexer_2_out[5], SW_IN[4:3], multiplexer_2_out[2:0]}
  or or_1 (or_1_out, and_2_out, async_w);
  Register register_1 (
    .D({2'b00, multiplexer_2_out[5], SW_IN[4:3], multiplexer_2_out[2:0]}), .en(or_1_out), .Q(OUT),
    .clk(WREG_CLK_RST[0]), .clr(WREG_CLK_RST[1]));
  // Probe on multiplexer_2_out[5]
  Multiplexer #(.enable("false")) multiplexer_1 (
    .in0(buffer_1_out), .in1(BUS_IN[5]), .out(multiplexer_2_out[5]), .sel(and_2_out));
  // Probe on multiplexer_2_out[2:0]
  Multiplexer #(.width(3), .enable("false")) multiplexer_2 (
    .in0(BUS_IN[2:0]), .in1(SW_IN[2:0]), .out(multiplexer_2_out[2:0]), .sel(SW_IN[5]));
  assign BUS_OUT = and_1_out ? OUT : 8'bz;  // Controlled_Buffer controlled_buffer_1
  buf buffer_1 (buffer_1_out, OUT[5]);
  // Probe on SW_IN[5]
endmodule

module PORTA_reg (
  input  [2:0] WREG_CLK_RST,
  input  [7:0] BUS_IN,
  input  [6:0] SYNCH_ADDRESS,
  input  [6:0] DIRECT_ADDRESS,
  input  [7:0] TRISA,
  input  [4:0] PIN_IN,
  output [7:0] BUS_OUT,
  output [7:0] OUT
);

  wire and_1_out, comparator_1_eq, not_1_out;
  wire [7:0] controlled_buffer_1_out;

  Comparator #(.width(7)) comparator_1 (.a(SYNCH_ADDRESS), .b(DIRECT_ADDRESS), .eq(comparator_1_eq));  // open: gt, lt
  assign controlled_buffer_1_out = comparator_1_eq ? BUS_IN : 8'bz;  // Controlled_Buffer controlled_buffer_1
  not not_1 (not_1_out, WREG_CLK_RST[2]);
  and and_1 (and_1_out, comparator_1_eq, not_1_out);
  assign BUS_OUT = and_1_out ? {3'b000, OUT[4:0]} : 8'bz;  // Controlled_Buffer controlled_buffer_2
  PORT_reg port_reg_1 (
    .Data_Bus_In(controlled_buffer_1_out[0]), .WR_Port(WREG_CLK_RST[2]), .TRIS(TRISA[0]),
    .I_O_pin(PIN_IN[0]), .I_O_pin_out(OUT[0]), .CLK(WREG_CLK_RST[0]));  // open: RD_Port
  PORT_reg port_reg_2 (
    .Data_Bus_In(controlled_buffer_1_out[1]), .WR_Port(WREG_CLK_RST[2]), .TRIS(TRISA[1]),
    .I_O_pin(PIN_IN[1]), .I_O_pin_out(OUT[1]), .CLK(WREG_CLK_RST[0]));  // open: RD_Port
  PORT_reg port_reg_3 (
    .Data_Bus_In(controlled_buffer_1_out[2]), .WR_Port(WREG_CLK_RST[2]), .TRIS(TRISA[2]),
    .I_O_pin(PIN_IN[2]), .I_O_pin_out(OUT[2]), .CLK(WREG_CLK_RST[0]));  // open: RD_Port
  PORT_reg port_reg_4 (
    .Data_Bus_In(controlled_buffer_1_out[3]), .WR_Port(WREG_CLK_RST[2]), .TRIS(TRISA[3]),
    .I_O_pin(PIN_IN[3]), .I_O_pin_out(OUT[3]), .CLK(WREG_CLK_RST[0]));  // open: RD_Port
  PORT_reg port_reg_5 (
    .Data_Bus_In(controlled_buffer_1_out[4]), .WR_Port(WREG_CLK_RST[2]), .TRIS(TRISA[4]),
    .I_O_pin(PIN_IN[4]), .I_O_pin_out(OUT[4]), .CLK(WREG_CLK_RST[0]));  // open: RD_Port

  assign OUT[7:5] = 3'b000;
endmodule

module PORTB_reg (
  input  [2:0] WREG_CLK_RST,
  input  [7:0] BUS_IN,
  input  [6:0] SYNCH_ADDRESS,
  input  [6:0] DIRECT_ADDRESS,
  input  [7:0] TRISB,
  input  [7:0] PIN_IN,
  output RBIF,
  output [7:0] BUS_OUT,
  output [7:0] OUT
);

  wire and_1_out, comparator_1_eq, not_1_out, port_change_reg_1_int, port_change_reg_2_int,
       port_change_reg_3_int, port_change_reg_4_int;
  wire [7:0] controlled_buffer_1_out;

  Comparator #(.width(7)) comparator_1 (.a(SYNCH_ADDRESS), .b(DIRECT_ADDRESS), .eq(comparator_1_eq));  // open: gt, lt
  Button button_1 ();  // open: out
  assign controlled_buffer_1_out = comparator_1_eq ? BUS_IN : 8'bz;  // Controlled_Buffer controlled_buffer_1
  not not_1 (not_1_out, WREG_CLK_RST[2]);
  and and_1 (and_1_out, comparator_1_eq, not_1_out);
  assign BUS_OUT = and_1_out ? OUT : 8'bz;  // Controlled_Buffer controlled_buffer_2
  Clock clock_1 ();  // open: out
  PORT_change_reg port_change_reg_1 (
    .Data_Bus_In(controlled_buffer_1_out[7]), .WR_Port(WREG_CLK_RST[2]), .TRIS(TRISB[7]),
    .RD_Port(and_1_out), .I_O_pin(PIN_IN[7]), .I_O_pin_out(OUT[7]), .INT(port_change_reg_1_int),
    .CLK(WREG_CLK_RST[0]));
  PORT_change_reg port_change_reg_2 (
    .Data_Bus_In(controlled_buffer_1_out[6]), .WR_Port(WREG_CLK_RST[2]), .TRIS(TRISB[6]),
    .RD_Port(and_1_out), .I_O_pin(PIN_IN[6]), .I_O_pin_out(OUT[6]), .INT(port_change_reg_2_int),
    .CLK(WREG_CLK_RST[0]));
  PORT_change_reg port_change_reg_3 (
    .Data_Bus_In(controlled_buffer_1_out[5]), .WR_Port(WREG_CLK_RST[2]), .TRIS(TRISB[5]),
    .RD_Port(and_1_out), .I_O_pin(PIN_IN[5]), .I_O_pin_out(OUT[5]), .INT(port_change_reg_3_int),
    .CLK(WREG_CLK_RST[0]));
  PORT_change_reg port_change_reg_4 (
    .Data_Bus_In(controlled_buffer_1_out[4]), .WR_Port(WREG_CLK_RST[2]), .TRIS(TRISB[4]),
    .RD_Port(and_1_out), .I_O_pin(PIN_IN[4]), .I_O_pin_out(OUT[4]), .INT(port_change_reg_4_int),
    .CLK(WREG_CLK_RST[0]));
  PORT_reg port_reg_1 (
    .Data_Bus_In(controlled_buffer_1_out[2]), .WR_Port(WREG_CLK_RST[2]), .TRIS(TRISB[2]),
    .RD_Port(and_1_out), .I_O_pin(PIN_IN[2]), .I_O_pin_out(OUT[2]), .CLK(WREG_CLK_RST[0]));
  PORT_reg port_reg_2 (
    .Data_Bus_In(controlled_buffer_1_out[3]), .WR_Port(WREG_CLK_RST[2]), .TRIS(TRISB[3]),
    .RD_Port(and_1_out), .I_O_pin(PIN_IN[3]), .I_O_pin_out(OUT[3]), .CLK(WREG_CLK_RST[0]));
  PORT_reg port_reg_3 (
    .Data_Bus_In(controlled_buffer_1_out[1]), .WR_Port(WREG_CLK_RST[2]), .TRIS(TRISB[1]),
    .RD_Port(and_1_out), .I_O_pin(PIN_IN[1]), .I_O_pin_out(OUT[1]), .CLK(WREG_CLK_RST[0]));
  PORT_reg port_reg_4 (
    .Data_Bus_In(controlled_buffer_1_out[0]), .WR_Port(WREG_CLK_RST[2]), .TRIS(TRISB[0]),
    .RD_Port(and_1_out), .I_O_pin(PIN_IN[0]), .I_O_pin_out(OUT[0]), .CLK(WREG_CLK_RST[0]));
  or or_1 (RBIF, port_change_reg_4_int, port_change_reg_3_int, port_change_reg_2_int, port_change_reg_1_int);
endmodule

module async_register (
  input  [6:0] SYNCH_ADDRESS,
  input  [7:0] BUS_IN,
  input  [7:0] AsynchronousW,
  input  [6:0] DIRECT_ADDRESS,
  input  [2:0] WREG_CLK_RST,
  input  WE_async,
  output [7:0] OUT,
  output [7:0] BUS_OUT
);

  wire and_1_out, and_2_out, comparator_1_eq, not_1_out, or_1_out;
  wire [7:0] DATA;

  Comparator #(.width(7)) comparator_1 (.a(SYNCH_ADDRESS), .b(DIRECT_ADDRESS), .eq(comparator_1_eq));  // open: gt, lt
  and and_1 (and_1_out, comparator_1_eq, WREG_CLK_RST[2]);
  and and_2 (and_2_out, comparator_1_eq, not_1_out);
  not not_1 (not_1_out, WREG_CLK_RST[2]);
  // Probe on DATA
  Register register_1 (.D(DATA), .en(or_1_out), .Q(OUT), .clk(WREG_CLK_RST[0]), .clr(WREG_CLK_RST[1]));
  or or_1 (or_1_out, and_1_out, WE_async);
  assign BUS_OUT = and_2_out ? OUT : 8'bz;  // Controlled_Buffer controlled_buffer_1
  Multiplexer #(.width(8), .enable("false")) multiplexer_1 (
    .in0(BUS_IN), .in1(AsynchronousW), .out(DATA), .sel(WE_async));
  // Probe on BUS_OUT
  // Probe on BUS_IN
  // Probe on AsynchronousW
endmodule

module PORT_reg (
  input  CLK,
  input  Data_Bus_In,
  input  I_O_pin,
  input  WR_Port,
  input  TRIS,
  input  RD_Port,
  output I_O_pin_out
);

  wire controlled_buffer_1_out, DATA_q, not_1_out, not_2_out;

  D_Flip_Flop DATA (.clk(CLK), .D(Data_Bus_In), .Q(DATA_q), .en(WR_Port));  // open: Qn, preset, reset
  assign controlled_buffer_1_out = not_1_out ? DATA_q : 1'bz;  // Controlled_Buffer controlled_buffer_1
  not not_1 (not_1_out, TRIS);
  assign controlled_buffer_1_out = TRIS ? I_O_pin : 1'bz;  // Controlled_Buffer controlled_buffer_2
  D_Flip_Flop DATA_2 (
    .clk(CLK), .D(controlled_buffer_1_out), .Q(I_O_pin_out), .en(not_2_out));  // open: Qn, preset, reset
  not not_2 (not_2_out, RD_Port);
endmodule

module PORT_change_reg (
  input  CLK,
  input  Data_Bus_In,
  input  I_O_pin,
  input  WR_Port,
  input  TRIS,
  input  RD_Port,
  output I_O_pin_out,
  output INT
);

  wire controlled_buffer_1_out, d_ff_2_q, DATA_q, not_1_out, not_2_out, xor_1_out;

  D_Flip_Flop DATA (.clk(CLK), .D(Data_Bus_In), .Q(DATA_q), .en(WR_Port));  // open: Qn, preset, reset
  not not_1 (not_1_out, RD_Port);
  assign controlled_buffer_1_out = TRIS ? I_O_pin : 1'bz;  // Controlled_Buffer controlled_buffer_1
  assign controlled_buffer_1_out = not_2_out ? DATA_q : 1'bz;  // Controlled_Buffer controlled_buffer_2
  not not_2 (not_2_out, TRIS);
  D_Flip_Flop d_ff_1 (
    .clk(CLK), .D(controlled_buffer_1_out), .Q(I_O_pin_out), .en(not_1_out));  // open: Qn, preset, reset
  xor xor_1 (xor_1_out, I_O_pin_out, d_ff_2_q);
  D_Flip_Flop d_ff_2 (.clk(CLK), .D(controlled_buffer_1_out), .Q(d_ff_2_q), .en(RD_Port));  // open: Qn, preset, reset
  and and_1 (INT, TRIS, xor_1_out);
endmodule
