// Logisim project APOLLO.circ as structural Verilog: 5 circuits, main circuit main
// DATA_BUS
module main (
);

  wire ACC_E, ALU_SEL, and_2_out, CLOCK, CLOCK_out, comparator_1_gt, comparator_1_lt, counter_1_carry, END,
       JMP, JMP_0, JMP_DBG, JMP_IF, JMP_PC, not_1_out, OE, or_2_out, REGW, s_r_ff_1_q, START_out, STOP_out,
       SWE;
  wire [0:0] RESET;
  wire [1:0] DATA_SEL;
  wire [3:0] ACCU, adder_1_cout, adder_1_out, counter_2_q, counter_2_q_2, counter_2_q_3, DATA, DATA_BUS,
       INPUT, OUTPUT, REGISTERS, RESULT, SW;
  wire [4:0] counter_1_q;
  wire [7:0] JMP_ADDRE, PC_q;
  wire [11:3] rom_3_data;

  Hex_Digit_Display hex_digit_display_1 (.value(DATA), .dp(1'b1));
  Hex_Digit_Display hex_digit_display_2 (.value(DATA_BUS), .dp(1'b1));
  Hex_Digit_Display hex_digit_display_3 (.value({2'b00, DATA[1:0]}), .dp(1'b1));
  Hex_Digit_Display hex_digit_display_4 (.value({2'b00, DATA[1:0]}), .dp(1'b1));
  Hex_Digit_Display hex_digit_display_5 (.value(REGISTERS), .dp(1'b1));
  Hex_Digit_Display hex_digit_display_6 (.value(ACCU), .dp(1'b1));
  Hex_Digit_Display hex_digit_display_7 (.value(ACCU), .dp(1'b1));
  Hex_Digit_Display hex_digit_display_8 (.value(ACCU), .dp(1'b1));
  Hex_Digit_Display hex_digit_display_9 (.value(INPUT), .dp(1'b1));
  Hex_Digit_Display hex_digit_display_10 (.value(RESULT), .dp(1'b1));
  LED WRITE (.in(REGW));
  LED OUTE (.in(OE));
  Hex_Digit_Display hex_digit_display_11 (.value(DATA_BUS), .dp(1'b1));
  Hex_Digit_Display hex_digit_display_12 (.value(SW), .dp(1'b1));
  Hex_Digit_Display hex_digit_display_13 (.value(REGISTERS), .dp(1'b1));
  Hex_Digit_Display hex_digit_display_14 (.value(OUTPUT), .dp(1'b1));
  Hex_Digit_Display hex_digit_display_15 (.value(JMP_ADDRE[7:4]), .dp(1'b1));
  LED u_JMP (.in(JMP_PC));
  LED ZERO (.in(SW[1]));
  LED CARRY (.in(SW[0]));
  Hex_Digit_Display hex_digit_display_16 (.value(counter_2_q_3), .dp(1'b1));
  Hex_Digit_Display hex_digit_display_17 (.value(counter_2_q_2), .dp(1'b1));
  Hex_Digit_Display hex_digit_display_18 (.value(JMP_ADDRE[3:0]), .dp(1'b1));
  Hex_Digit_Display hex_digit_display_19 (.value(counter_2_q), .dp(1'b1));
  Counter #(.trigger("falling")) PC (
    .load(JMP_PC), .D(JMP_ADDRE), .count(counter_1_carry), .Q(PC_q), .carry(END), .clk(CLOCK), .clr(RESET[0]));
  Counter #(.width(1), .max('h1)) counter_1 (
    .Q(counter_1_q[0]), .carry(counter_1_carry), .clk(CLOCK), .clr(RESET[0]));  // open: load, D, count
  Counter #(.width(12), .max('hfff)) counter_2 (
    .Q({counter_2_q_3, counter_2_q_2, counter_2_q}), .clk(CLOCK), .clr(RESET[0]));  // open: load, D, count, carry
  or or_1 (JMP_PC, JMP, JMP_DBG);
  assign JMP_ADDRE = JMP_DBG ? 8'h4 : 8'bz;  // Controlled_Buffer controlled_buffer_1
  Button u_RESET (.out(RESET[0]));
  Clock u_CLOCK (.out(CLOCK_out));
  Button START (.out(START_out));
  Button STOP (.out(STOP_out));
  Button JUMP_DBG (.out(JMP_DBG));
  ROM #(.addrWidth(5), .dataWidth(12)) rom_1 ();  // open: addr, data, sel
  not not_1 (not_1_out, JMP_DBG);
  assign JMP_ADDRE = not_1_out ? {DATA, ACCU} : 8'bz;  // Controlled_Buffer controlled_buffer_2
  ROM rom_2 (.addr(PC_q), .data({counter_1_q[4:1], DATA}), .sel(1'b1));
  ROM #(.addrWidth(5), .dataWidth(12)) rom_3 (
    .addr(counter_1_q),
    .data({rom_3_data[11:10], JMP_IF, JMP_0, REGW, SWE, ACC_E, ALU_SEL, rom_3_data[3], OE, DATA_SEL}),
    .sel(1'b1));
  and and_1 (CLOCK, CLOCK_out, s_r_ff_1_q);
  S_R_Flip_Flop s_r_ff_1 (.Q(s_r_ff_1_q), .preset(START_out), .reset(or_2_out), .en(1'b1));  // open: S, clk, R, Qn
  or or_2 (or_2_out, STOP_out, END);
  ROM rom_4 ();  // open: addr, data, sel
  or or_3 (JMP, JMP_0, and_2_out);
  and and_2 (and_2_out, JMP_IF, adder_1_cout[1]);
  _4bits_registersx4 u_REGISTERS (
    .DATA(ACCU), .ADDR(DATA[1:0]), .CLK_RESET({CLOCK, RESET[0]}), .W(REGW), .OUT(REGISTERS));
  Multiplexer #(.select(2), .width(4), .disabled(0), .enable("false")) multiplexer_1 (
    .in0(DATA), .in1(REGISTERS), .in2(INPUT), .out(DATA_BUS), .sel(DATA_SEL));  // open: in3
  Comparator #(.width(4)) comparator_1 (
    .a(ACCU), .b(DATA_BUS), .gt(comparator_1_gt), .eq(adder_1_cout[1]), .lt(comparator_1_lt));
  Multiplexer #(.select(2), .width(4), .enable("false")) multiplexer_2 (
    .in0(4'b0000), .in1(4'b0001), .in2(4'b0010), .in3(4'b0011), .out(INPUT), .sel(DATA[1:0]));
  Adder #(.width(4)) adder_1 (.a(ACCU), .b(DATA_BUS), .out(adder_1_out), .cin(SW[0]), .cout(adder_1_cout[0]));
  Register #(.width(4), .trigger("high")) STATUS (.D(adder_1_cout), .en(SWE), .Q(SW), .clk(CLOCK), .clr(RESET[0]));
  _4bits_registersx4 OUTPUT_REG (.DATA(ACCU), .ADDR(DATA[1:0]), .CLK_RESET({CLOCK, RESET[0]}), .W(OE), .OUT(OUTPUT));
  Multiplexer #(.width(4), .enable("false")) multiplexer_3 (
    .in0(DATA_BUS), .in1(adder_1_out), .out(RESULT), .sel(ALU_SEL));
  Register #(.width(4)) u_ACCU (.D(RESULT), .en(ACC_E), .Q(ACCU), .clk(CLOCK), .clr(RESET[0]));

  // Other names for the same wires on the sheet: PORT[1:0] = DATA[1:0]; PORT_HEX[1:0] = DATA[1:0];
  //   REG_HEX[1:0] = DATA[1:0]; REG_SEL[1:0] = DATA[1:0]; RESET[1] = CLOCK

  // Notes on the sheet:
  //   OUTPUT
  //   DATA MANAGMENT
  //   COMPUTATION
  //   REGISTERS
  //   PROM
  //   Program counter and sequencer
  //   contents of rom_1 (hex, n*v repeats v):
  //   0 0 100 4*0 20 1 21 1 81 11 31 20 30 1 51 0 50 2 22 0 5
  //   contents of rom_2 (hex, n*v repeats v):
  //   0 3f 1f
  //   contents of rom_3 (hex, n*v repeats v):
  //   0 0 100 4*0 20 1 21 1 81 11 31 20 30 1 51 0 50 2 22 0 5
  //   Control
  //   PROGRAM
  //   contents of rom_4 (hex, n*v repeats v):
  //   0 a1 51 a2 61 b0
  //   Jump managment
  //   Registers
  //   Data managment
  //   Arithmetic Logic Unit
  //   Input/Output
endmodule

module _4_data_selector (
  input  [3:0] I1,
  input  [3:0] I2,
  input  [3:0] I3,
  input  [3:0] I4,
  input  [1:0] sel,
  output [3:0] O
);

  wire decoder_1_out0, decoder_1_out1, decoder_1_out2, decoder_1_out3;

  Decoder #(.select(2)) decoder_1 (
    .out0(decoder_1_out0), .out1(decoder_1_out1), .out2(decoder_1_out2), .out3(decoder_1_out3), .sel(sel),
    .en(1'b1));
  assign O = decoder_1_out0 ? I1 : 4'bz;  // Controlled_Buffer controlled_buffer_1
  assign O = decoder_1_out2 ? I3 : 4'bz;  // Controlled_Buffer controlled_buffer_2
  assign O = decoder_1_out1 ? I2 : 4'bz;  // Controlled_Buffer controlled_buffer_3
  assign O = decoder_1_out3 ? I4 : 4'bz;  // Controlled_Buffer controlled_buffer_4
endmodule

module _4bits_registersx4 (
  input  [3:0] DATA,
  input  [1:0] ADDR,
  input  [1:0] CLK_RESET,
  input  W,
  output [3:0] OUT
);

  wire decoder_1_out0, decoder_1_out1, decoder_1_out2, decoder_1_out3, decoder_2_out0, decoder_2_out1,
       decoder_2_out2, decoder_2_out3;
  wire [3:0] register_1_q, register_2_q, register_3_q, register_4_q;

  Hex_Digit_Display hex_digit_display_1 (.value(DATA), .dp(1'b1));
  Decoder #(.select(2), .enable("false")) decoder_1 (
    .out0(decoder_1_out0), .out1(decoder_1_out1), .out2(decoder_1_out2), .out3(decoder_1_out3), .sel(ADDR));
  Decoder #(.select(2), .disabled(0)) decoder_2 (
    .out0(decoder_2_out0), .out1(decoder_2_out1), .out2(decoder_2_out2), .out3(decoder_2_out3), .sel(ADDR),
    .en(W));
  Register #(.width(4), .trigger("high")) register_1 (
    .D(DATA), .en(decoder_2_out3), .Q(register_1_q), .clk(CLK_RESET[1]), .clr(CLK_RESET[0]));
  assign OUT = decoder_1_out3 ? register_1_q : 4'bz;  // Controlled_Buffer controlled_buffer_1
  assign OUT = decoder_1_out2 ? register_2_q : 4'bz;  // Controlled_Buffer controlled_buffer_2
  Register #(.width(4), .trigger("high")) register_2 (
    .D(DATA), .en(decoder_2_out2), .Q(register_2_q), .clk(CLK_RESET[1]), .clr(CLK_RESET[0]));
  assign OUT = decoder_1_out1 ? register_3_q : 4'bz;  // Controlled_Buffer controlled_buffer_3
  Register #(.width(4), .trigger("high")) register_3 (
    .D(DATA), .en(decoder_2_out1), .Q(register_3_q), .clk(CLK_RESET[1]), .clr(CLK_RESET[0]));
  assign OUT = decoder_1_out0 ? register_4_q : 4'bz;  // Controlled_Buffer controlled_buffer_4
  Hex_Digit_Display hex_digit_display_2 (.value(OUT), .dp(1'b1));
  Register #(.width(4), .trigger("high")) register_4 (
    .D(DATA), .en(decoder_2_out0), .Q(register_4_q), .clk(CLK_RESET[1]), .clr(CLK_RESET[0]));
endmodule

module ALU (
  input  [3:0] I1,
  input  [3:0] I2,
  input  C_IN,
  input  B_IN,
  input  [3:0] SEL,
  output [3:0] OUT,
  output out_7,
  output out_8,
  output C_OUT,
  output B_OUT
);

  wire [3:0] adder_1_out, and_1_out, buffer_1_out, not_1_out, or_1_out, shifter_1_out, shifter_2_out,
       subtractor_1_out, xor_1_out;

  Comparator #(.width(4)) comparator_1 (.a(I2), .b(I1), .gt(out_8), .eq(out_7));  // open: lt
  Adder #(.width(4)) adder_1 (.a(I2), .b(I1), .out(adder_1_out), .cin(C_IN), .cout(C_OUT));
  Subtractor #(.width(4)) subtractor_1 (.a(I2), .b(I1), .out(subtractor_1_out), .bin(B_IN), .bout(B_OUT));
  assign or_1_out = I1 | I2;  // OR_Gate or_1, 4 bits wide
  assign and_1_out = I1 & I2;  // AND_Gate and_1, 4 bits wide
  assign xor_1_out = I1 ^ I2;  // XOR_Gate xor_1, 4 bits wide
  assign not_1_out = ~I1;  // NOT_Gate not_1, 4 bits wide
  assign buffer_1_out = I1;  // Buffer buffer_1, 4 bits wide
  Shifter #(.width(4), .shift("rl")) shifter_1 (.in(I1), .\dist ({1'b0, C_IN}), .out(shifter_1_out));
  Shifter #(.width(4), .shift("rl")) shifter_2 (.in(I2), .\dist ({1'b0, C_IN}), .out(shifter_2_out));
  Multiplexer #(.select(4), .width(4), .enable("false")) multiplexer_1 (
    .in0(shifter_2_out), .in1(shifter_1_out), .in2(buffer_1_out), .in3(not_1_out), .in4(xor_1_out),
    .in5(or_1_out), .in6(and_1_out), .in7(subtractor_1_out), .in8(adder_1_out), .out(OUT), .sel(SEL));  // open: in9, in10, in11, in12, in13, in14, in15
endmodule

module tester (
);

  wire alu_1_b_out, alu_1_c_out, alu_1_out_7, alu_1_out_8, const_out, count_out, s_r_ff_1_q, s_r_ff_1_qn,
       WRITE_out;
  wire [1:0] controlled_buffer_1_out, counter_1_q, RESET_out;
  wire [3:0] alu_1_out, multiplexer_1_out, n4_data_selector_1_o, n4bits_registersx4_1_out;

  _4_data_selector u_4_data_selector_1 (
    .sel(2'b11), .I1(4'b1010), .I2(4'b1011), .I3(4'b1100), .I4(4'b1101), .O(n4_data_selector_1_o));
  Hex_Digit_Display hex_digit_display_1 (.value(n4_data_selector_1_o), .dp(1'b1));
  Hex_Digit_Display hex_digit_display_2 (.value(multiplexer_1_out), .dp(1'b1));
  Multiplexer #(.select(2), .width(4)) multiplexer_1 (
    .in0(4'b1010), .in1(4'b1011), .in2(4'b1100), .out(multiplexer_1_out), .sel(2'b11), .en(1'b1));  // open: in3
  S_R_Flip_Flop s_r_ff_1 (
    .Q(s_r_ff_1_q), .Qn(s_r_ff_1_qn), .preset(count_out), .reset(const_out));  // open: S, clk, R, en
  Button \const  (.out(const_out));
  Button count (.out(count_out));
  assign controlled_buffer_1_out = s_r_ff_1_qn ? 2'b00 : 2'bz;  // Controlled_Buffer controlled_buffer_1
  Counter #(.width(2), .max('h3)) counter_1 (
    .Q(counter_1_q), .clk(RESET_out[1]), .clr(RESET_out[0]));  // open: load, D, count, carry
  assign controlled_buffer_1_out = s_r_ff_1_q ? counter_1_q : 2'bz;  // Controlled_Buffer controlled_buffer_2
  Button WRITE (.out(WRITE_out));
  Button RESET (.out(RESET_out[0]));
  Clock CLK_TEST (.out(RESET_out[1]));
  _4bits_registersx4 u_4bits_registersx4_1 (
    .DATA(4'b0011), .ADDR(controlled_buffer_1_out), .CLK_RESET(RESET_out), .W(WRITE_out),
    .OUT(n4bits_registersx4_1_out));
  ALU alu_1 (
    .I1(4'b1000), .I2(4'b0111), .C_IN(1'b0), .B_IN(1'b0), .SEL(4'b1001), .out_7(alu_1_out_7),
    .out_8(alu_1_out_8), .C_OUT(alu_1_c_out), .B_OUT(alu_1_b_out), .OUT(alu_1_out));
  LED led_1 (.in(alu_1_out_7));
  LED led_2 (.in(alu_1_b_out));
  LED led_3 (.in(alu_1_out_8));
  LED led_4 (.in(alu_1_c_out));
  Hex_Digit_Display hex_digit_display_3 (.value(n4bits_registersx4_1_out), .dp(1'b1));
  Hex_Digit_Display hex_digit_display_4 (.value(alu_1_out), .dp(1'b1));
endmodule
