// Logisim project appolo181.circ as structural Verilog: 4 circuits, main circuit appolo181
module appolo181 (
);

  wire [1:0] clk_rst;
  wire [3:0] ACCU, DATA, DATA_BUS, START_out;
  wire [7:0] cpu_1_ram_address, INSTRUCTION;
  wire [9:0] INSTR_STATES;
  wire [23:0] counter_1_q;
  wire [31:0] DATA_STATES, MEMORY;

  // Probe on 4'b0000
  // Probe on 4'b0011
  // Probe on 4'b1100
  // Probe on 4'b1101
  Button START (.out(START_out[0]));
  Button STOP (.out(START_out[1]));
  Button RESET (.out(START_out[2]));
  Clock clock_1 (.out(START_out[3]));
  // Probe on cpu_1_ram_address
  CPU cpu_1 (
    .RAM_DATA(INSTRUCTION), .INPUTS(16'hdc30), .RAM_ADDRESS(cpu_1_ram_address), .COMMAND(START_out),
    .JUMP_STATE(INSTR_STATES),
    .MACHINE_DATA({DATA_STATES[31:20], DATA, ACCU, DATA_STATES[11:8], DATA_BUS, DATA_STATES[3:0]}),
    .out_4(clk_rst), .MEMORY(MEMORY));
  RAM #(.bus("asynch")) ram_1 (.addr(cpu_1_ram_address), .data(INSTRUCTION));  // open: sel, ld, clr
  // Probe on DATA_STATES[27:24]
  // Probe on ACCU
  // Probe on INSTRUCTION[7:4]
  // Probe on DATA
  // Probe on DATA_BUS
  // Probe on INSTRUCTION[3:0]
  // Probe on DATA_STATES[23:20]
  // Probe on DATA_STATES[3:0]
  // Probe on MEMORY[15:0]
  // Probe on INSTR_STATES[9:2]
  // Probe on DATA_BUS
  // Probe on DATA_STATES[11:8]
  // Probe on MEMORY[31:16]
  LED JUMP (.in(INSTR_STATES[1]));
  // Probe on counter_1_q
  Counter #(.width(24), .max('hffffff)) counter_1 (
    .Q(counter_1_q), .clk(clk_rst[1]), .clr(clk_rst[0]));  // open: load, D, count, carry
  RAM #(.addrWidth(24), .dataWidth(10), .bus("asynch")) ram_2 (
    .addr(counter_1_q), .data(INSTR_STATES), .ld(1'b0), .clr(clk_rst[0]));  // open: sel
  RAM #(.addrWidth(24), .dataWidth(32), .bus("asynch")) ram_3 (
    .addr(counter_1_q),
    .data({DATA_STATES[31:20], DATA, ACCU, DATA_STATES[11:8], DATA_BUS, DATA_STATES[3:0]}), .ld(1'b0),
    .clr(clk_rst[0]));  // open: sel

  // Other names for the same wires on the sheet: RESULT[3:0] = DATA_STATES[3:0];
  //   DATA_STATES (some bits) = {DATA, ACCU, DATA_BUS}; SW[3:0] = DATA_STATES[11:8]; REG[3:0] = DATA_STATES[23:20];
  //   INPUT[3:0] = DATA_STATES[27:24]; OUTPUT[3:0] = DATA_STATES[31:28]; jump = INSTR_STATES[1];
  //   JUMP_ADDRESS[7:0] = INSTR_STATES[9:2]

  // Notes on the sheet:
  //   Command
  //   Input
  //   Program
  //   INSTRUCTION
  //   DATA MANAGMENT
  //   COMPUTATION
  //   MEMORY
  //   Monitoring
  //   States Stored
  //   Instruction state
  //   Data states
endmodule

module CPU (
  input  [15:0] INPUTS,
  input  [7:0] RAM_DATA,
  input  [3:0] COMMAND,
  output [1:0] out_4,
  output [7:0] RAM_ADDRESS,
  output [9:0] JUMP_STATE,
  output [31:0] MEMORY,
  output [31:0] MACHINE_DATA
);

  wire acc_e, and_2_out, \end , jmp, jmp0, jmpIF, oe, or_1_out, reg_w, s_r_ff_1_q, SEQ_carry, sw_e;
  wire [0:0] SEQ_q;
  wire [1:0] dat_sel;
  wire [3:0] alu_1_sw_out, alu_sel, TEST;

  Button button_1 (.out(JUMP_STATE[0]));
  and and_1 (out_4[1], COMMAND[3], s_r_ff_1_q);
  S_R_Flip_Flop s_r_ff_1 (.Q(s_r_ff_1_q), .preset(COMMAND[0]), .reset(or_1_out));  // open: S, clk, R, Qn, en
  or or_1 (or_1_out, COMMAND[1], \end );
  Button START (.out(TEST[0]));
  Button STOP (.out(TEST[1]));
  Button RESET (.out(TEST[2]));
  Clock clock_1 (.out(TEST[3]));
  // Probe on JUMP_STATE[9:2]
  Counter #(.ongoal("stay")) PC (
    .load(JUMP_STATE[1]), .D(JUMP_STATE[9:2]), .count(SEQ_carry), .Q(RAM_ADDRESS), .carry(\end ),
    .clk(out_4[1]), .clr(COMMAND[2]));
  Counter #(.width(1), .max('h1)) SEQ (
    .Q(SEQ_q[0]), .carry(SEQ_carry), .clk(out_4[1]), .clr(COMMAND[2]));  // open: load, D, count
  or or_2 (jmp, jmp0, and_2_out);
  and and_2 (and_2_out, jmpIF, MACHINE_DATA[11]);
  Multiplexer #(.width(8), .enable("false")) multiplexer_1 (
    .in0(8'h7), .in1({MACHINE_DATA[15:12], RAM_DATA[3:0]}), .out(JUMP_STATE[9:2]), .sel(jmp));
  or or_3 (JUMP_STATE[1], jmp, JUMP_STATE[0]);
  // Probe on RAM_DATA[7:4]
  // Probe on MACHINE_DATA[3:0]
  // Probe on alu_1_sw_out
  // Probe on RAM_DATA
  // Probe on {dat_sel, oe, acc_e, sw_e, reg_w, jmp0, jmpIF, alu_sel}
  ROM #(.addrWidth(5), .dataWidth(12)) rom_1 (
    .addr({RAM_DATA[7:4], SEQ_q[0]}), .data({dat_sel, oe, acc_e, sw_e, reg_w, jmp0, jmpIF, alu_sel}));  // open: sel
  Register #(.width(4), .trigger("falling")) register_1 (
    .D(MACHINE_DATA[3:0]), .en(acc_e), .Q(MACHINE_DATA[15:12]), .clk(out_4[1]), .clr(COMMAND[2]));
  // Probe on MACHINE_DATA[15:12]
  Register #(.width(4), .trigger("falling")) register_2 (
    .D(alu_1_sw_out), .en(sw_e), .Q(MACHINE_DATA[11:8]), .clk(out_4[1]), .clr(COMMAND[2]));
  // Probe on MACHINE_DATA[7:4]
  // Probe on alu_sel
  // Probe on MACHINE_DATA[3:0]
  ALU alu_1 (
    .OUT(MACHINE_DATA[3:0]), .I1(MACHINE_DATA[15:12]), .I2(MACHINE_DATA[7:4]), .SW_OUT(alu_1_sw_out),
    .SEL(alu_sel), .SW_IN(MACHINE_DATA[11:8]));
  Multiplexer #(.select(2), .width(4), .enable("false")) multiplexer_2 (
    .in0(INPUTS[3:0]), .in1(INPUTS[7:4]), .in2(INPUTS[11:8]), .in3(INPUTS[15:12]), .out(MACHINE_DATA[27:24]),
    .sel(RAM_DATA[1:0]));
  // Probe on MACHINE_DATA[27:24]
  // Probe on MACHINE_DATA[23:20]
  // Probe on RAM_DATA[3:0]
  // Probe on dat_sel
  Multiplexer #(.select(2), .width(4), .disabled(0), .enable("false")) multiplexer_3 (
    .in0(MACHINE_DATA[27:24]), .in1(RAM_DATA[3:0]), .in2(MACHINE_DATA[23:20]), .out(MACHINE_DATA[7:4]),
    .sel(dat_sel));  // open: in3
  // Probe on MACHINE_DATA[7:4]
  // Probe on MACHINE_DATA[31:28]
  // Probe on RAM_DATA[1:0]
  _4bits_registersx4 u_4bits_registersx4_1 (
    .DATA(MACHINE_DATA[15:12]), .ADDR(RAM_DATA[1:0]), .CLK_RESET({out_4[1], COMMAND[2]}), .W(reg_w),
    .OUT(MACHINE_DATA[23:20]), .MEM(MEMORY[15:0]));
  _4bits_registersx4 u_4bits_registersx4_2 (
    .DATA(MACHINE_DATA[15:12]), .ADDR(RAM_DATA[1:0]), .CLK_RESET({out_4[1], COMMAND[2]}), .W(oe),
    .OUT(MACHINE_DATA[31:28]), .MEM(MEMORY[31:16]));

  assign MACHINE_DATA[19:16] = RAM_DATA[3:0];
  assign out_4[0] = COMMAND[2];

  // Other names for the same wires on the sheet: clk_rst[1:0] = {out_4[1], COMMAND[2]}; rst = COMMAND[2];
  //   start = COMMAND[0]; stop = COMMAND[1]; clk = COMMAND[3]; INSTRUCTION[7:0] = RAM_DATA;
  //   OPCODE[3:0] = RAM_DATA[7:4]; jmp_dbg = JUMP_STATE[0]; jump = JUMP_STATE[1]; JUMP_ADDRESS[7:0] = JUMP_STATE[9:2];
  //   RESULT[3:0] = MACHINE_DATA[3:0]; DATA_BUS[3:0] = MACHINE_DATA[7:4]; SW[3:0] = MACHINE_DATA[11:8];
  //   ACCU[3:0] = MACHINE_DATA[15:12]; DATA[3:0] = RAM_DATA[3:0]; REG[3:0] = MACHINE_DATA[23:20];
  //   INPUT[3:0] = MACHINE_DATA[27:24]; OUTPUT[3:0] = MACHINE_DATA[31:28]; REGS[15:0] = MEMORY[15:0];
  //   OUTPUTS[15:0] = MEMORY[31:16]; RAMaddress[7:0] = RAM_ADDRESS

  // Notes on the sheet:
  //   Start/Stop unit
  //   Jump managment
  //   Instruction Control
  //   Program counter
  //   PROM
  //   Jump and ALU
  //   contents of rom_1 (hex, n*v repeats v):
  //   400 400 420 400 410 400 800 840 800 900 800 880 801 981 400 500 400 480 401 581 0 100 600 400
  //   Data Managment
  //   Bus selection
  //   Outputs
endmodule

module _4bits_registersx4 (
  input  [3:0] DATA,
  input  [1:0] ADDR,
  input  [1:0] CLK_RESET,
  input  W,
  output [15:0] MEM,
  output [3:0] OUT
);

  wire decoder_1_out0, decoder_1_out1, decoder_1_out2, decoder_1_out3;

  Decoder #(.select(2), .disabled(0)) decoder_1 (
    .out0(decoder_1_out0), .out1(decoder_1_out1), .out2(decoder_1_out2), .out3(decoder_1_out3), .sel(ADDR),
    .en(W));
  Register #(.width(4), .trigger("falling")) register_1 (
    .D(DATA), .en(decoder_1_out3), .Q(MEM[15:12]), .clk(CLK_RESET[1]), .clr(CLK_RESET[0]));
  Register #(.width(4), .trigger("falling")) register_2 (
    .D(DATA), .en(decoder_1_out2), .Q(MEM[11:8]), .clk(CLK_RESET[1]), .clr(CLK_RESET[0]));
  Register #(.width(4), .trigger("falling")) register_3 (
    .D(DATA), .en(decoder_1_out1), .Q(MEM[7:4]), .clk(CLK_RESET[1]), .clr(CLK_RESET[0]));
  Multiplexer #(.select(2), .width(4), .enable("false")) multiplexer_1 (
    .in0(MEM[3:0]), .in1(MEM[7:4]), .in2(MEM[11:8]), .in3(MEM[15:12]), .out(OUT), .sel(ADDR));
  Register #(.width(4), .trigger("falling")) register_4 (
    .D(DATA), .en(decoder_1_out0), .Q(MEM[3:0]), .clk(CLK_RESET[1]), .clr(CLK_RESET[0]));
endmodule

module ALU (
  input  [3:0] SW_IN,
  input  [3:0] I1,
  input  [3:0] I2,
  input  [3:0] SEL,
  output [3:0] OUT,
  output [3:0] SW_OUT
);

  wire adder_1_cout, comparator_2_eq, comparator_3_eq, comparator_4_eq, not_1_out, not_2_out, not_3_out,
       subtractor_1_bout;
  wire [1:0] comparator_1_gt;
  wire [3:0] adder_1_out, and_1_out, buffer_1_out, not_4_out, or_1_out, shifter_1_out, shifter_2_out,
       subtractor_1_out, xor_1_out;

  Comparator #(.width(4)) comparator_1 (.a(I2), .b(I1), .gt(comparator_1_gt[0]), .eq(comparator_1_gt[1]));  // open: lt
  not not_1 (not_1_out, comparator_2_eq);
  Comparator #(.width(4)) comparator_2 (.a(SEL), .b(4'b0000), .eq(comparator_2_eq));  // open: gt, lt
  not not_2 (not_2_out, comparator_3_eq);
  Comparator #(.width(4)) comparator_3 (.a(SEL), .b(4'b0001), .eq(comparator_3_eq));  // open: gt, lt
  not not_3 (not_3_out, comparator_4_eq);
  Comparator #(.width(4)) comparator_4 (.a(SEL), .b(4'b0010), .eq(comparator_4_eq));  // open: gt, lt
  Multiplexer #(.width(2), .enable("false")) multiplexer_1 (
    .in0(comparator_1_gt), .in1(SW_IN[3:2]), .out(SW_OUT[3:2]), .sel(not_1_out));
  Multiplexer #(.enable("false")) multiplexer_2 (.in0(SW_IN[1]), .in1(adder_1_cout), .out(SW_OUT[1]), .sel(not_2_out));
  Adder #(.width(4)) adder_1 (.a(I2), .b(I1), .out(adder_1_out), .cin(SW_IN[1]), .cout(adder_1_cout));
  Multiplexer #(.enable("false")) multiplexer_3 (
    .in0(SW_IN[0]), .in1(subtractor_1_bout), .out(SW_OUT[0]), .sel(not_3_out));
  Subtractor #(.width(4)) subtractor_1 (
    .a(I2), .b(I1), .out(subtractor_1_out), .bin(SW_IN[0]), .bout(subtractor_1_bout));
  assign and_1_out = I1 & I2;  // AND_Gate and_1, 4 bits wide
  assign or_1_out = I1 | I2;  // OR_Gate or_1, 4 bits wide
  assign not_4_out = ~I1;  // NOT_Gate not_4, 4 bits wide
  assign xor_1_out = I1 ^ I2;  // XOR_Gate xor_1, 4 bits wide
  assign buffer_1_out = I1;  // Buffer buffer_1, 4 bits wide
  Shifter #(.width(4), .shift("rl")) shifter_1 (.in(I1), .\dist ({1'b0, SW_IN[1]}), .out(shifter_1_out));
  Shifter #(.width(4), .shift("rl")) shifter_2 (.in(I2), .\dist ({1'b0, SW_IN[1]}), .out(shifter_2_out));
  Multiplexer #(.select(4), .width(4), .enable("false")) multiplexer_4 (
    .in0(I2), .in1(adder_1_out), .in2(subtractor_1_out), .in3(and_1_out), .in4(or_1_out), .in5(xor_1_out),
    .in6(not_4_out), .in7(shifter_1_out), .in8(buffer_1_out), .in9(shifter_2_out), .out(OUT), .sel(SEL));  // open: in10, in11, in12, in13, in14, in15
endmodule
