// Logisim project mult.circ as structural Verilog: 1 circuit, main circuit main
module main (
);

  wire comparator_1_eq, not_1_out;
  wire [1:0] clk_rst;
  wire [3:0] adder_1_out, adder_2_out, counter_1_q, register_1_q;

  // Probe on 4'b0011
  // Probe on 4'b0101
  Button RESET (.out(clk_rst[0]));
  Clock clock_1 (.out(clk_rst[1]));
  Adder #(.width(4)) adder_1 (.a(4'b0011), .b(4'b0001), .out(adder_1_out));  // open: cin, cout
  Counter #(.width(4), .max('hf)) counter_1 (
    .count(not_1_out), .Q(counter_1_q), .clk(clk_rst[1]), .clr(clk_rst[0]));  // open: load, D, carry
  Comparator #(.width(4)) comparator_1 (.a(adder_1_out), .b(counter_1_q), .eq(comparator_1_eq));  // open: gt, lt
  not not_1 (not_1_out, comparator_1_eq);
  Adder #(.width(4)) adder_2 (.a(register_1_q), .b(4'b0101), .out(adder_2_out));  // open: cin, cout
  Register #(.width(4), .trigger("falling")) register_1 (
    .D(adder_2_out), .en(not_1_out), .Q(register_1_q), .clk(clk_rst[1]), .clr(clk_rst[0]));
  // Probe on register_1_q
endmodule
